# Fritzing sketch cartoon camera schematic (saved by Fritzing 0.9.3b)
breadboards: 1

parts:
  Raspberry_Pi_1 = Raspberry Pi 3 [part_number=RPI-3-V1.2]
  SHUTTER = Round Pushbutton
  R1 = Resistor [tolerance=±5% resistance=220 package="0402 [SMD]"]
  Part1 = Thermal Printer
  VCC1 = 4 x AAA Battery Mount
  S2 = Toggle Switch [package=THT]

nets:
  N1: Raspberry_Pi_1.3v3, SHUTTER.leg1
  N2: Raspberry_Pi_1.GIPO4, SHUTTER.leg0, R1.Pin_1
  GND: Raspberry_Pi_1.GND, R1.Pin_0, Part1.GND, S2.COM
  N3: Raspberry_Pi_1.GIPO15, Part1.TXD
  N4: Raspberry_Pi_1.5V, Part1.VH, VCC1.+
